# Fritzing sketch breadboardlayoutDualRGB (saved by Fritzing 0.9.3b)
circuit board: 8.46667cm x 5.64444cm

parts:
  Power_plug1_12v = Power plug
  FET1 = STP16NF06 N-Channel Power MOSFET
  FET2 = STP16NF06 N-Channel Power MOSFET
  FET3 = STP16NF06 N-Channel Power MOSFET
  RGB_Strip_LED2 = RGB Strip LED
  U1 = ESP8266-12e_smt [part_number=ESP8266-12E]
  Power_plug2 = Power plug
  R2 = Resistor [tolerance=±5% resistance=1k package="0805 [SMD]"]
  R1 = Resistor [tolerance=±5% resistance=1k package="0805 [SMD]"]
  R3 = Resistor [tolerance=±5% resistance=1k package="0805 [SMD]"]
  LM1117 = V_REG_LD1117VXX [package=78xxl]
  RGB_Strip_LED3 = RGB Strip LED
  Power_plug2_12v = Power plug
  FET4 = STP16NF06 N-Channel Power MOSFET
  FET5 = STP16NF06 N-Channel Power MOSFET
  FET6 = STP16NF06 N-Channel Power MOSFET
  R4 = Resistor [tolerance=±5% resistance=1k package="0805 [SMD]"]
  R5 = Resistor [tolerance=±5% resistance=1k package="0805 [SMD]"]
  R6 = Resistor [tolerance=±5% resistance=1k package="0805 [SMD]"]
  FET7 = STP16NF06 N-Channel Power MOSFET

nets:
  N1: Power_plug1_12v.GND, FET1.source, FET2.source, FET3.source
  N2: Power_plug1_12v.VCC, RGB_Strip_LED2.Common_Connect#4
  N3: FET1.gate, R1.Pin_1
  N4: FET1.drain, RGB_Strip_LED2.Blue_Connect#5
  N5: FET2.gate, R2.Pin_1
  N6: FET2.drain, RGB_Strip_LED2.Red_Connect#6
  N7: FET3.gate, R3.Pin_1
  N8: FET3.drain, RGB_Strip_LED2.Green_Connect#7
  N9: U1.CH_PD, U1.VCC, LM1117.OUT
  N10: U1.GPIO_16, R2.Pin_0
  N11: U1.GPIO_14, R3.Pin_0
  N12: U1.GPIO_12, R1.Pin_0
  N13: U1.GPIO_13, FET7.gate
  N14: U1.GPIO_10, R4.Pin_0
  GND: U1.GND, U1.GPIO_15, Power_plug2.GND, LM1117.GND
  N15: U1.GPIO_4, R6.Pin_0
  N16: U1.GPIO_5, R5.Pin_0
  N17: Power_plug2.VCC, LM1117.IN
  N18: RGB_Strip_LED3.Common_Connect#4, Power_plug2_12v.VCC
  N19: RGB_Strip_LED3.Blue_Connect#5, FET4.drain
  N20: RGB_Strip_LED3.Red_Connect#6, FET5.drain
  N21: RGB_Strip_LED3.Green_Connect#7, FET6.drain
  N22: Power_plug2_12v.GND, FET4.source, FET5.source, FET6.source
  N23: FET4.gate, R4.Pin_1
  N24: FET5.gate, R5.Pin_1
  N25: FET6.gate, R6.Pin_1

notes:
  5v
  12v
  I've used power supply unit from a PC
  NOTICE!
  so it has a common ground.
  If you are going to use separate power sources
  don't forget to unite ground (connect black wires)
  LM1117
  power supply enable

custom parts:
  STP16NF06 N-Channel Power MOSFET: STP16NF06 N-channel Power MOSFET
  RGB Strip LED: A tri-color Strip LED with red, green and blue. Pin order: red - common cathode - blue - green
  ESP8266-12e_smt: These are the first series of modules made with the ESP8266 by the third-party manufacturer AI-Thinker and remain the most widely available. They are collectively referred to as "ESP-xx modules" and to form a workable development system require additional components, especially a serial TTL-to-USB adapter (sometimes called a USB-to-UART bridge) and an external 3.3V power supply. ESP8266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
