# Fritzing sketch breadboardlayoutRGB (saved by Fritzing 0.9.3b)
circuit board: 8.46667cm x 5.64444cm

parts:
  Power_plug1 = Power plug
  FET1 = STP16NF06 N-Channel Power MOSFET
  FET2 = STP16NF06 N-Channel Power MOSFET
  FET3 = STP16NF06 N-Channel Power MOSFET
  RGB_Strip_LED2 = RGB Strip LED
  U1 = ESP8266-12e_smt [part_number=ESP8266-12E]
  Power_plug2 = Power plug
  R2 = Resistor [tolerance=±5% resistance=1k package="0805 [SMD]"]
  R1 = Resistor [tolerance=±5% resistance=1k package="0805 [SMD]"]
  R3 = Resistor [tolerance=±5% resistance=1k package="0805 [SMD]"]

nets:
  N1: Power_plug1.GND, FET1.source, FET2.source, FET3.source
  N2: Power_plug1.VCC, RGB_Strip_LED2.Common_Connect#4
  N3: FET1.gate, R1.Pin_1
  N4: FET1.drain, RGB_Strip_LED2.Blue_Connect#5
  N5: FET2.gate, R2.Pin_1
  N6: FET2.drain, RGB_Strip_LED2.Red_Connect#6
  N7: FET3.gate, R3.Pin_1
  N8: FET3.drain, RGB_Strip_LED2.Green_Connect#7
  VCC: U1.CH_PD, U1.VCC, Power_plug2.VCC
  N9: U1.GPIO_14, R3.Pin_0
  N10: U1.GPIO_12, R2.Pin_0
  N11: U1.GPIO_13, R1.Pin_0
  GND: U1.GND, U1.GPIO_15, Power_plug2.GND

notes:
  3.3v
  12v
  I've used power supply unit from a PC
  NOTICE!
  so it has a common ground.
  If you are going to use separate power sources
  don't forget to unite ground (connect black wires)

custom parts:
  STP16NF06 N-Channel Power MOSFET: STP16NF06 N-channel Power MOSFET
  RGB Strip LED: A tri-color Strip LED with red, green and blue. Pin order: red - common cathode - blue - green
  ESP8266-12e_smt: These are the first series of modules made with the ESP8266 by the third-party manufacturer AI-Thinker and remain the most widely available. They are collectively referred to as "ESP-xx modules" and to form a workable development system require additional components, especially a serial TTL-to-USB adapter (sometimes called a USB-to-UART bridge) and an external 3.3V power supply. ESP8266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
